// Logisim project PRESENT.circ as structural Verilog: 12 circuits, main circuit main
module main (
  input  [31:0] in_1,
  input  [31:0] in_2,
  input  [15:0] in_3,
  input  [31:0] in_4,
  input  [31:0] in_5
);

  wire add_round_key_layer_1_p2, add_round_key_layer_1_p4;
  wire [31:0] p_box_layer_1_out_3, p_box_layer_1_out_4, s_box_layer_1_out_3, s_box_layer_1_out_4;

  // Add_Round_Key_Layer add_round_key_layer_1: pin names not known; wires that end beside it: in_1, add_round_key_layer_1_p2, in_2, add_round_key_layer_1_p4
  // Multiplexer multiplexer_1: pin names not known; wires that end beside it: add_round_key_layer_1_p2, add_round_key_layer_1_p4
  S_box_layer s_box_layer_1 (.out_3(s_box_layer_1_out_3), .out_4(s_box_layer_1_out_4));  // open: M32_63, M0_31
  P_box_layer p_box_layer_1 (
    .in_1(s_box_layer_1_out_3), .in_2(s_box_layer_1_out_4), .out_3(p_box_layer_1_out_3),
    .out_4(p_box_layer_1_out_4));
  Add_Round_Key_Layer add_round_key_layer_2 (
    .in_1(p_box_layer_1_out_3), .in_2(p_box_layer_1_out_4));  // open: out_5, out_6, in_3, in_4
  Key_Schedule key_schedule_1 ();  // open: in_1, in_2, in_3, out_5, out_6, out_7, Round_Clock
endmodule

module S_box (
  input  [3:0] S_input,
  output [3:0] S_output
);

  Multiplexer #(.select(4), .width(4), .enable("false")) multiplexer_1 (
    .in0(4'b1100), .in1(4'b0101), .in2(4'b0110), .in3(4'b1011), .in4(4'b1001), .in5(4'b0000), .in6(4'b1010),
    .in7(4'b1101), .in8(4'b0011), .in9(4'b1110), .in10(4'b1111), .in11(4'b1000), .in12(4'b0100),
    .in13(4'b0111), .in14(4'b0001), .in15(4'b0010), .out(S_output), .sel(S_input));
endmodule

module Add_Round_Key (
  input  [31:0] in_1,
  input  [31:0] in_2,
  output [31:0] out_3
);

  assign out_3 = in_1 ^ in_2;  // XOR_Gate xor_1, 32 bits wide
endmodule

module S_box_layer (
  input  [31:0] M32_63,
  input  [31:0] M0_31,
  output [31:0] out_3,
  output [31:0] out_4
);

  S_box w15 (.S_input(M32_63[31:28]), .S_output(out_3[31:28]));
  S_box w14 (.S_input(M32_63[27:24]), .S_output(out_3[27:24]));
  S_box w13 (.S_input(M32_63[23:20]), .S_output(out_3[23:20]));
  S_box w12 (.S_input(M32_63[19:16]), .S_output(out_3[19:16]));
  S_box w10 (.S_input(M32_63[11:8]), .S_output(out_3[11:8]));
  S_box w11 (.S_input(M32_63[15:12]), .S_output(out_3[15:12]));
  S_box w9 (.S_input(M32_63[7:4]), .S_output(out_3[7:4]));
  S_box w8 (.S_input(M32_63[3:0]), .S_output(out_3[3:0]));
  S_box w7 (.S_input(M0_31[31:28]), .S_output(out_4[31:28]));
  S_box w6 (.S_input(M0_31[27:24]), .S_output(out_4[27:24]));
  S_box w5 (.S_input(M0_31[23:20]), .S_output(out_4[23:20]));
  S_box w4 (.S_input(M0_31[19:16]), .S_output(out_4[19:16]));
  S_box w2 (.S_input(M0_31[11:8]), .S_output(out_4[11:8]));
  S_box w3 (.S_input(M0_31[15:12]), .S_output(out_4[15:12]));
  S_box w1 (.S_input(M0_31[7:4]), .S_output(out_4[7:4]));
  S_box w0 (.S_input(M0_31[3:0]), .S_output(out_4[3:0]));
endmodule

module Add_Round_Key_Layer (
  input  [31:0] in_1,
  input  [31:0] in_2,
  input  [31:0] in_3,
  input  [31:0] in_4,
  output [31:0] out_5,
  output [31:0] out_6
);

  Add_Round_Key add_round_key_1 (.in_1(in_1), .out_3(out_5), .in_2(in_3));
  Add_Round_Key add_round_key_2 (.in_1(in_2), .out_3(out_6), .in_2(in_4));
endmodule

module P_box_4_bit (
  input  [3:0] in_1,
  output out_2,
  output out_3,
  output out_4,
  output out_5
);


  assign out_2 = in_1[3];
  assign out_3 = in_1[2];
  assign out_4 = in_1[1];
  assign out_5 = in_1[0];
endmodule

module P_box_16_bit (
  input  [15:0] in_1,
  output [3:0] out_2,
  output [3:0] out_3,
  output [3:0] out_4,
  output [3:0] out_5
);

  P_box_4_bit p_box_4_bit_1 (
    .in_1(in_1[15:12]), .out_2(out_2[3]), .out_3(out_3[3]), .out_4(out_4[3]), .out_5(out_5[3]));
  P_box_4_bit p_box_4_bit_2 (.in_1(in_1[11:8]), .out_2(out_2[2]), .out_3(out_3[2]), .out_4(out_4[2]), .out_5(out_5[2]));
  P_box_4_bit p_box_4_bit_3 (.in_1(in_1[7:4]), .out_2(out_2[1]), .out_3(out_3[1]), .out_4(out_4[1]), .out_5(out_5[1]));
  P_box_4_bit p_box_4_bit_4 (.in_1(in_1[3:0]), .out_2(out_2[0]), .out_3(out_3[0]), .out_4(out_4[0]), .out_5(out_5[0]));
endmodule

module P_box_layer (
  input  [31:0] in_1,
  input  [31:0] in_2,
  output [31:0] out_3,
  output [31:0] out_4
);

  P_box_16_bit p_box_16_bit_1 (
    .in_1(in_1[31:16]), .out_2(out_3[31:28]), .out_3(out_3[15:12]), .out_4(out_4[31:28]), .out_5(out_4[15:12]));
  P_box_16_bit p_box_16_bit_2 (
    .in_1(in_1[15:0]), .out_2(out_3[27:24]), .out_3(out_3[11:8]), .out_4(out_4[27:24]), .out_5(out_4[11:8]));
  P_box_16_bit p_box_16_bit_3 (
    .in_1(in_2[31:16]), .out_2(out_3[23:20]), .out_3(out_3[7:4]), .out_4(out_4[23:20]), .out_5(out_4[7:4]));
  P_box_16_bit p_box_16_bit_4 (
    .in_1(in_2[15:0]), .out_2(out_3[19:16]), .out_3(out_3[3:0]), .out_4(out_4[19:16]), .out_5(out_4[3:0]));
endmodule

module Key_Schedule (
  input  [15:0] in_1,
  input  [31:0] in_2,
  input  [31:0] in_3,
  input  [4:0] Round_Clock,
  output [15:0] out_5,
  output [31:0] out_6,
  output [31:0] out_7
);

  wire [15:0] left_shift_by_61_bits_80_bit_1_out_6;
  wire [31:0] left_shift_by_61_bits_80_bit_1_out_4, left_shift_by_61_bits_80_bit_1_out_5;

  Left_shift_by_61_bits__80_bit left_shift_by_61_bits_80_bit_1 (
    .in_1(in_1), .in_2(in_2), .in_3(in_3), .out_6(left_shift_by_61_bits_80_bit_1_out_6),
    .out_4(left_shift_by_61_bits_80_bit_1_out_4), .out_5(left_shift_by_61_bits_80_bit_1_out_5));
  Pass_via_S_box_and_XOR_with_Round_Counter pass_via_s_box_and_xor_with_round_counter_1 (
    .in_1(left_shift_by_61_bits_80_bit_1_out_6), .in_2(left_shift_by_61_bits_80_bit_1_out_4),
    .in_3(left_shift_by_61_bits_80_bit_1_out_5), .out_7(out_5), .out_5(out_6), .out_6(out_7),
    .in_4(Round_Clock));
endmodule

module Left_shift_by_61_bits__80_bit (
  input  [15:0] in_1,
  input  [31:0] in_2,
  input  [31:0] in_3,
  output [31:0] out_4,
  output [31:0] out_5,
  output [15:0] out_6
);


  assign out_4 = {in_3[2:0], in_1, in_2[31:19]};
  assign out_5 = {in_2[18:0], in_3[31:19]};
  assign out_6 = in_3[18:3];
endmodule

module Pass_via_S_box_and_XOR_with_Round_Counter (
  input  [15:0] in_1,
  input  [31:0] in_2,
  input  [31:0] in_3,
  input  [4:0] in_4,
  output [31:0] out_5,
  output [31:0] out_6,
  output [15:0] out_7
);

  S_box s_box_1 (.S_input(in_1[15:12]), .S_output(out_7[15:12]));
  assign out_6[19:15] = in_3[19:15] ^ in_4;  // XOR_Gate xor_1, 5 bits wide

  assign out_5 = in_2;
  assign {out_6[31:20], out_6[14:0]} = {in_3[31:20], in_3[14:0]};
  assign out_7[11:0] = in_1[11:0];
endmodule

module Extract_Key (
  input  [15:0] in_1,
  input  [31:0] in_2,
  input  [31:0] in_3,
  output [31:0] out_4,
  output [31:0] out_5
);


  assign out_4 = {in_1, in_2[31:16]};
  assign out_5 = {in_2[15:0], in_3[31:16]};
endmodule
